# Fritzing sketch Arduino Uno to Raspberry Pi (saved by Fritzing 0.9.2b)
breadboards: 1

parts:
  Part1 = Arduino Uno (Rev3)
  Raspberry_Pi1 = Raspberry Pi B rev2
  IC1 = IC, DIP package, 14 pins [chip_label=SN74AHC125N]

nets:
  N1: Part1.D0/RX, IC1.pin2
  N2: Part1.D1/TX, IC1.pin5
  GND: Part1.GND, Raspberry_Pi1.GND, IC1.pin7
  VIN: Part1.VIN, Raspberry_Pi1.5V
  N3: Raspberry_Pi1.3V3, IC1.pin14
  N4: Raspberry_Pi1.GPIO_14, IC1.pin3
  N5: Raspberry_Pi1.GPIO_15, IC1.pin6
